// Logisim project LC-2200-32.circ as structural Verilog: 6 circuits, main circuit Processor
module Processor (
);

  wire Clock, Clr, DrALU, DrEnInt, DrMEM, DrOFF, DrPC, DrReg, IE, IntAck, intergenerator_1_intout, LdA, LdB,
       LdEnInt, LdIR, ldIV, LdMAR, LdPC, LdZ, not_1_out, not_2_out, onInt, register_1_q, WrMEM, WrREG, Z,
       ZeroDetectOut;
  wire [1:0] comparator_1_lt, FUNC, RegSel;
  wire [3:0] IR_q, IR_q_3, IR_q_4, Opcode, Reg_num;
  wire [23:0] controlled_buffer_1_out, MAR_q;
  wire [31:0] A_q, B_q, bit_extender_1_out, multiplexer_1_out, PC_q, ram_1_data, registers_1_data_out,
       ZeroDetect;
  wire [31:4] IR_q_2;
  wire [31:24] controlled_buffer_1_out_2;

  Multiplexer #(.select(2), .width(32), .enable("false")) multiplexer_1 (
    .in0({controlled_buffer_1_out_2, controlled_buffer_1_out}), .in1(32'ha),
    .in2({controlled_buffer_1_out_2, controlled_buffer_1_out}),
    .in3({controlled_buffer_1_out_2, controlled_buffer_1_out}), .out(multiplexer_1_out), .sel(comparator_1_lt));
  and and_1 (comparator_1_lt[1], comparator_1_lt[0], ldIV);
  Comparator #(.width(32)) comparator_1 (.a(PC_q), .b(32'ha), .lt(comparator_1_lt[0]));  // open: gt, eq
  Register #(.width(32)) PC (.D(multiplexer_1_out), .en(LdPC), .Q(PC_q), .clk(Clock), .clr(Clr));
  assign {controlled_buffer_1_out_2, controlled_buffer_1_out} = DrPC ? PC_q : 32'bz;  // Controlled_Buffer controlled_buffer_1
  State_Machine state_machine_1 (
    .DrEnInt(DrEnInt), .LdEnInt(LdEnInt), .IntAck(IntAck), .Clock(Clock), .OpCode(Opcode), .Z(Z),
    .intOut(onInt), .IE(IE), .DrREG(DrReg), .DrMEM(DrMEM), .DrALU(DrALU), .DrPC(DrPC), .DrOFF(DrOFF),
    .LdPC(LdPC), .LdIR(LdIR), .LdMAR(LdMAR), .LdA(LdA), .LdB(LdB), .LdZ(LdZ), .WrREG(WrREG), .WrMEM(WrMEM),
    .RegSel(RegSel), .ALU_FUNC(FUNC));
  Register #(.width(1)) Z_Register (.D(ZeroDetectOut), .en(LdZ), .Q(Z), .clk(Clock), .clr(Clr));
  Register #(.width(32)) A (
    .D({controlled_buffer_1_out_2, controlled_buffer_1_out}), .en(LdA), .Q(A_q), .clk(Clock), .clr(Clr));
  ALU alu_1 (.FUNC(FUNC), .INPUT_A(A_q), .INPUT_B(B_q), .out_4(ZeroDetect));
  Register #(.width(32)) B (
    .D({controlled_buffer_1_out_2, controlled_buffer_1_out}), .en(LdB), .Q(B_q), .clk(Clock), .clr(Clr));
  assign {controlled_buffer_1_out_2, controlled_buffer_1_out} = DrALU ? ZeroDetect : 32'bz;  // Controlled_Buffer controlled_buffer_2
  Clock clock_1 (.out(Clock));
  Button button_1 (.out(Clr));
  Registers registers_1 (
    .WrReg(WrREG), .RegSel(Reg_num), .Data_In({controlled_buffer_1_out_2, controlled_buffer_1_out}),
    .Clock(Clock), .ClearRegFile(Clr), .Data_Out(registers_1_data_out));
  assign {controlled_buffer_1_out_2, controlled_buffer_1_out} = DrReg ? registers_1_data_out : 32'bz;  // Controlled_Buffer controlled_buffer_3
  Register #(.width(1)) register_1 (.D(DrEnInt), .en(LdEnInt), .Q(register_1_q), .clk(Clock));  // open: clr
  assign bit_extender_1_out = {{31{1'b0}}, 1'b1};  // Bit_Extender bit_extender_1
  assign {controlled_buffer_1_out_2, controlled_buffer_1_out} = IntAck ? bit_extender_1_out : 32'bz;  // Controlled_Buffer controlled_buffer_4
  not not_1 (not_1_out, IntAck);
  and and_2 (IE, not_1_out, register_1_q);
  Register #(.width(24)) MAR (.D(controlled_buffer_1_out), .en(LdMAR), .Q(MAR_q), .clk(Clock), .clr(Clr));
  not not_2 (not_2_out, WrMEM);
  RAM #(.addrWidth(24), .dataWidth(32), .bus("separate")) ram_1 (
    .addr(MAR_q), .din({controlled_buffer_1_out_2, controlled_buffer_1_out}), .data(ram_1_data), .str(WrMEM),
    .clk(Clock), .ld(not_2_out), .clr(Clr));  // open: sel
  assign {controlled_buffer_1_out_2, controlled_buffer_1_out} = DrMEM ? ram_1_data : 32'bz;  // Controlled_Buffer controlled_buffer_5
  and and_3 (onInt, IE, intergenerator_1_intout);
  Intergenerator intergenerator_1 (.IntOut(intergenerator_1_intout), .CLK(Clock));
  Register #(.width(32)) IR (
    .D({controlled_buffer_1_out_2, controlled_buffer_1_out}), .en(LdIR),
    .Q({Opcode, IR_q_4, IR_q_3, IR_q_2[31], IR_q_2[18:4], IR_q}), .clk(Clock), .clr(Clr));
  Multiplexer #(.select(2), .width(4), .enable("false")) multiplexer_2 (
    .in0(IR_q_4), .in1(IR_q_3), .in2(IR_q), .in3(4'b1100), .out(Reg_num), .sel(RegSel));
  assign {controlled_buffer_1_out_2, controlled_buffer_1_out} = DrOFF ? {{13{IR_q_2[31]}}, IR_q_2[18:4], IR_q} : 32'bz;  // Controlled_Buffer controlled_buffer_6
  Comparator #(.width(32), .mode("unsigned")) comparator_2 (
    .a(ZeroDetect), .b({32{1'b0}}), .eq(ZeroDetectOut));  // open: gt, lt
  Register #(.width(1)) register_2 (
    .D(intergenerator_1_intout), .en(intergenerator_1_intout), .Q(ldIV), .clk(Clock));  // open: clr

  // Notes on the sheet:
  //   <- I use the mux
  //   with the input dependent on
  //   the output of a register I made
  //   to tell me when interrupts have been
  //   enabled AND if the PC is < 10
  //   when I access the IV
  //   so that it does not get overwritten
  //   The output of the IE reg is ANDed with an inverted IntAck since I only want interrupts to be enabled until they are acknlowedged
  //   This is my IE register. 
  //   00 = RX
  //   01 = RY
  //   10 = RZ
  //   Sign extend the value of the interrupt. Drive onto bus only when IntAck is asserted
  //   Register I made to tell me when interrupts have been enabled at least once. This helps me preserve the PC value when the IV value is loaded.
endmodule

module ALU (
  input  [31:0] INPUT_A,
  input  [31:0] INPUT_B,
  input  [1:0] FUNC,
  output [31:0] out_4
);

  wire [31:0] adder_1_out, adder_2_out, nand_1_out, subtractor_1_out;

  Adder #(.width(32)) adder_1 (.a(INPUT_A), .b(INPUT_B), .out(adder_1_out));  // open: cin, cout
  assign nand_1_out = ~(INPUT_A & INPUT_B);  // NAND_Gate nand_1, 32 bits wide
  Multiplexer #(.select(2), .width(32), .enable("false")) multiplexer_1 (
    .in0(adder_1_out), .in1(nand_1_out), .in2(subtractor_1_out), .in3(adder_2_out), .out(out_4), .sel(FUNC));
  Subtractor #(.width(32)) subtractor_1 (.a(INPUT_A), .b(INPUT_B), .out(subtractor_1_out));  // open: bin, bout
  Adder #(.width(32)) adder_2 (.a(INPUT_A), .b(32'h1), .out(adder_2_out));  // open: cin, cout
endmodule

module State_Machine (
  input  Clock,
  input  [3:0] OpCode,
  input  Z,
  input  intOut,
  input  IE,
  output DrREG,
  output DrMEM,
  output DrALU,
  output DrPC,
  output DrOFF,
  output LdPC,
  output LdIR,
  output LdMAR,
  output LdA,
  output LdB,
  output DrEnInt,
  output LdEnInt,
  output LdZ,
  output WrREG,
  output IntAck,
  output WrMEM,
  output [1:0] RegSel,
  output [1:0] ALU_FUNC
);

  wire and_1_out, chkZ, OpTest, or_1_out, register_1_q;
  wire [0:0] controlled_buffer_1_out;
  wire [1:0] multiplexer_1_out;
  wire [5:0] multiplexer_2_out, register_2_q, rom_1_data, rom_2_data, rom_3_data, rom_4_data;

  or or_1 (or_1_out, intOut, register_1_q);
  Register #(.width(1)) register_1 (.D(intOut), .en(or_1_out), .Q(register_1_q), .clk(Clock));  // open: clr
  Register #(.width(6)) register_2 (.D(multiplexer_2_out), .en(Clock), .Q(register_2_q), .clk(Clock));  // open: clr
  Multiplexer #(.width(2), .enable("false")) multiplexer_1 (
    .in0({chkZ, OpTest}), .in1(2'b11), .out(multiplexer_1_out), .sel(and_1_out));
  Multiplexer #(.select(2), .width(6), .enable("false")) multiplexer_2 (
    .in0(rom_1_data), .in1(rom_2_data), .in2(rom_3_data), .in3(rom_4_data), .out(multiplexer_2_out),
    .sel(multiplexer_1_out));
  and and_1 (and_1_out, IE, register_1_q);
  assign controlled_buffer_1_out[0] = IE ? register_1_q : 1'bz;  // Controlled_Buffer controlled_buffer_1
  ROM #(.addrWidth(6), .dataWidth(28)) rom_1 (
    .addr(register_2_q),
    .data({IntAck, DrEnInt, LdEnInt, chkZ, OpTest, ALU_FUNC, RegSel, WrMEM, WrREG, LdZ, LdB, LdA, LdMAR, LdIR, LdPC, DrOFF, DrPC, DrALU, DrMEM, DrREG, rom_1_data}));  // open: sel
  ROM #(.addrWidth(4), .dataWidth(6)) rom_2 (.addr(OpCode), .data(rom_2_data));  // open: sel
  ROM #(.addrWidth(2), .dataWidth(6)) rom_3 (.addr({1'b0, Z}), .data(rom_3_data));  // open: sel
  ROM #(.addrWidth(2), .dataWidth(6)) rom_4 (
    .addr({1'b0, controlled_buffer_1_out[0]}), .data(rom_4_data));  // open: sel

  // Notes on the sheet:
  //   If IE, load the ROM so it can be sent to the MUX.
  //   contents of rom_1 (hex, n*v repeats v):
  //   6201 1082 e00900 21a0204 8000800 6000000 2000000 6180840 4*0 8404d 10804e 20100 84050 108051 220100
  //   84053 8414 20100 84056 8417 2118 20080 8405a 841b 211c 40040 405e 8805f 410120 1000000 4222 8423 900
  //   a0225 840 26 840 28
  //   Reg keeps track of INT assertions. Loads value if INT is currently being fired or if INT recently fired.
  //   Mux determines if INT has been asserted. Output becomes signal select of the main mux for the roms.
  //   I only want to use the INT rom if IE AND if an interrupt happened.
  //   contents of rom_2 (hex, n*v repeats v):
  //   c f 12 15 19 1d 24 26 a b 5 6 7 8 9
  //   contents of rom_3 (hex, n*v repeats v):
  //   0 21
  //   contents of rom_4 (hex, n*v repeats v):
  //   1 3
endmodule

// 0?
module Zero_Detection (
  input  [31:0] In,
  output Out
);

  Comparator #(.width(32), .mode("unsigned")) comparator_1 (.a(In), .b({32{1'b0}}), .eq(Out));  // open: gt, lt
endmodule

// Reg File
module Registers (
  input  [31:0] Data_In,
  input  WrReg,
  input  [3:0] RegSel,
  input  Clock,
  input  ClearRegFile,
  output [31:0] Data_Out
);

  wire and_1_out, and_2_out, and_3_out, and_4_out, and_5_out, and_6_out, and_7_out, and_8_out, and_9_out,
       and_10_out, and_11_out, and_12_out, and_13_out, and_14_out, and_15_out, and_16_out, decoder_1_out0,
       decoder_1_out1, decoder_1_out2, decoder_1_out3, decoder_1_out4, decoder_1_out5, decoder_1_out6,
       decoder_1_out7, decoder_1_out8, decoder_1_out9, decoder_1_out10, decoder_1_out11, decoder_1_out12,
       decoder_1_out13, decoder_1_out14, decoder_1_out15;
  wire [31:0] a0, a1, a2, at, k0, pr, ra, s0, s1, s2, sp, t0, t1, t2, v0, zero;

  Decoder #(.select(4), .enable("false")) decoder_1 (
    .out0(decoder_1_out0), .out1(decoder_1_out1), .out2(decoder_1_out2), .out3(decoder_1_out3),
    .out4(decoder_1_out4), .out5(decoder_1_out5), .out6(decoder_1_out6), .out7(decoder_1_out7),
    .out8(decoder_1_out8), .out9(decoder_1_out9), .out10(decoder_1_out10), .out11(decoder_1_out11),
    .out12(decoder_1_out12), .out13(decoder_1_out13), .out14(decoder_1_out14), .out15(decoder_1_out15),
    .sel(RegSel));
  and and_1 (and_1_out, decoder_1_out0, WrReg);
  and and_2 (and_2_out, decoder_1_out1, WrReg);
  and and_3 (and_3_out, decoder_1_out2, WrReg);
  and and_4 (and_4_out, decoder_1_out3, WrReg);
  and and_5 (and_5_out, decoder_1_out4, WrReg);
  and and_6 (and_6_out, decoder_1_out5, WrReg);
  and and_7 (and_7_out, decoder_1_out6, WrReg);
  and and_8 (and_8_out, decoder_1_out7, WrReg);
  and and_9 (and_9_out, decoder_1_out8, WrReg);
  and and_10 (and_10_out, decoder_1_out9, WrReg);
  and and_11 (and_11_out, decoder_1_out10, WrReg);
  and and_12 (and_12_out, decoder_1_out11, WrReg);
  and and_13 (and_13_out, decoder_1_out12, WrReg);
  and and_14 (and_14_out, decoder_1_out13, WrReg);
  and and_15 (and_15_out, decoder_1_out14, WrReg);
  and and_16 (and_16_out, decoder_1_out15, WrReg);
  Register #(.width(32)) u_zero (.D(Data_In), .en(and_1_out), .Q(zero), .clk(Clock), .clr(1'b1));
  Register #(.width(32)) u_at (.D(Data_In), .en(and_2_out), .Q(at), .clk(Clock), .clr(ClearRegFile));
  Register #(.width(32)) u_v0 (.D(Data_In), .en(and_3_out), .Q(v0), .clk(Clock), .clr(ClearRegFile));
  Register #(.width(32)) u_a0 (.D(Data_In), .en(and_4_out), .Q(a0), .clk(Clock), .clr(ClearRegFile));
  Register #(.width(32)) u_a1 (.D(Data_In), .en(and_5_out), .Q(a1), .clk(Clock), .clr(ClearRegFile));
  Register #(.width(32)) u_a2 (.D(Data_In), .en(and_6_out), .Q(a2), .clk(Clock), .clr(ClearRegFile));
  Register #(.width(32)) u_t0 (.D(Data_In), .en(and_7_out), .Q(t0), .clk(Clock), .clr(ClearRegFile));
  Register #(.width(32)) u_t1 (.D(Data_In), .en(and_8_out), .Q(t1), .clk(Clock), .clr(ClearRegFile));
  Register #(.width(32)) u_t2 (.D(Data_In), .en(and_9_out), .Q(t2), .clk(Clock), .clr(ClearRegFile));
  Register #(.width(32)) u_s0 (.D(Data_In), .en(and_10_out), .Q(s0), .clk(Clock), .clr(ClearRegFile));
  Register #(.width(32)) u_s1 (.D(Data_In), .en(and_11_out), .Q(s1), .clk(Clock), .clr(ClearRegFile));
  Register #(.width(32)) u_s2 (.D(Data_In), .en(and_12_out), .Q(s2), .clk(Clock), .clr(ClearRegFile));
  Register #(.width(32)) u_k0 (.D(Data_In), .en(and_13_out), .Q(k0), .clk(Clock), .clr(ClearRegFile));
  Register #(.width(32)) u_sp (.D(Data_In), .en(and_14_out), .Q(sp), .clk(Clock), .clr(ClearRegFile));
  Register #(.width(32)) u_pr (.D(Data_In), .en(and_15_out), .Q(pr), .clk(Clock), .clr(ClearRegFile));
  Register #(.width(32)) u_ra (.D(Data_In), .en(and_16_out), .Q(ra), .clk(Clock), .clr(ClearRegFile));
  Multiplexer #(.select(4), .width(32), .enable("false")) multiplexer_1 (
    .in0(zero), .in1(at), .in2(v0), .in3(a0), .in4(a1), .in5(a2), .in6(t0), .in7(t1), .in8(t2), .in9(s0),
    .in10(s1), .in11(s2), .in12(k0), .in13(sp), .in14(pr), .in15(ra), .out(Data_Out), .sel(RegSel));

  // Other names for the same wires on the sheet: Din[31:0] = Data_In; en = WrReg
endmodule

module Intergenerator (
  input  CLK,
  output IntOut
);

  wire register_2_q;
  wire [10:0] adder_1_out, register_1_q;

  Adder #(.width(11)) adder_1 (.a(11'h1), .b(register_1_q), .out(adder_1_out));  // open: cin, cout
  Register #(.width(11)) register_1 (.D(adder_1_out), .en(1'b1), .Q(register_1_q), .clk(CLK), .clr(register_2_q));
  Comparator #(.width(11), .mode("unsigned")) comparator_1 (
    .a(11'h200), .b(register_1_q), .eq(IntOut));  // open: gt, lt
  Register #(.width(1)) register_2 (.D(IntOut), .en(1'b1), .Q(register_2_q), .clk(CLK), .clr(register_2_q));
endmodule
